# Fritzing sketch From_the_example_code_CD4051 (saved by Fritzing 0.9.5d)
breadboards: 1

parts:
  Composant1 = Arduino Uno (Rev3) - ICSP
  CD1 = CD4051
  CD2 = CD4051
  U3 = POT [package=pot_mammoth]
  U6 = POT [package=pot_mammoth]
  U7 = POT [package=pot_mammoth]
  U8 = POT [package=pot_mammoth]
  S1 = SWITCH-MOMENTARY-2 [package=tactile_switch_smd-2]
  S2 = SWITCH-MOMENTARY-2 [package=tactile_switch_tall]
  R1 = Resistor [tolerance=±5% resistance=10k package="2010 [SMD]"]

nets:
  N1: Composant1.A0, CD1.In/Out, CD2.In/Out
  N2: Composant1.A1, U8.A
  N3: Composant1.A2, U7.A
  VSS: Composant1.GND, CD1.VEE, CD1.VSS, CD2.VEE, CD2.VSS, U3.S, U6.E, U7.S, U8.S, S1.2, S2.1, R1.Pin_1
  N4: Composant1.D8, CD1.Input_A, CD2.Input_A
  N5: Composant1.D9_PWM, CD1.Input_B, CD2.Input_B
  N6: Composant1.D10_PWM/SS, CD1.Input_C, CD2.Input_C
  N7: Composant1.D2, S2.2
  N8: Composant1.D6_PWM, CD1.Inhibit
  N9: Composant1.D7, CD2.Inhibit
  VDD: Composant1.5V, CD1.VDD, CD2.VDD, U3.E, U6.S, U7.E, U8.E, S1.1
  N10: CD1.Chan_0, U3.A
  N11: CD2.Chan_6, R1.Pin_0
  N12: CD2.Chan_7, U6.A
